# Fritzing sketch Board (saved by Fritzing 0.9.3b)

parts:
  LED1 = RGB LED (com. cathode, rgb) [package="5 mm [THT]"]
  S1 = Round Pushbutton
  J1 = Piezo Speaker
  Part2 = PowerBoost 500 Charger
  BAT1 = Battery Holders [package=lipo-1100mAh]
  Part3 = Arduino Pro Mini v13

nets:
  N1: LED1.red_anode, Part3.D4
  GND: LED1.common_cathode, J1.pin1, Part2.GND, BAT1.-, Part3.GND
  N2: LED1.green_anode, Part3.D2
  N3: S1.leg0, Part3.D9_PWM
  N4: S1.leg1, Part3.D8
  N5: J1.pin2, Part3.D7
  N6: Part2.VBAT_OUT, BAT1.+
  N7: Part2.5.0V, Part3.VCC
